// Digital circuit main.dig as structural Verilog
module main (
  input  clk
);

  wire A_WR_DB, ACC_WR_DB, ADDR_RS0_A, ADDR_RS0_B, ADDR_RS0_C, ADDR_RS0_D, ADDR_RS1_A, ADDR_RS1_B,
       ADDR_RS1_C, ADDR_RS1_D, ALU_A_IN_A, ALU_A_IN_B, ALU_B_IN_A, ALU_B_IN_B, ALU_C_IN_A, ALU_C_IN_B,
       ALU_D_IN_A, ALU_D_IN_B, and_1_out, B_WR_DB, C_WR_DB, D_WR_DB, demultiplexer_1_out_0,
       demultiplexer_1_out_1, imm16, IR0_RD, IR1_RD, IR2_RD, MEM_OE, MEM_WE, nand_1_out, not_1_out, or_1_out,
       or_2_out, PC_H_RD, PC_INC, PC_L_RD, PC_ovf, PC_WR_ABUS, RD_R_rs0, RD_R_rs1, RD_R_vvvv, REG_A_RD,
       REG_ACC_RD, REG_B_RD, REG_C_RD, REG_D_RD, RS_WR_ABUS, SP_DEC, SP_H_RD, SP_H_WR_DB, SP_INC, SP_L_RD,
       SP_L_WR_DB, SP_ovf, SP_WR_ABUS, STORE_ACC, STORE_FLAG, undriven, WR_R_rs0, WR_R_rs1, WR_R_vvvv;
  wire [1:0] AB_WR_DEV, ll;
  wire [2:0] DB_WR_DEV, ooo, REG_RD, rs0, rs1, vvv;
  wire [3:0] alu_1_flags_2, Flag_q;
  wire [7:0] A_q, ACC_q, alu_1_out, B_q, C_q, D_q, driver_3_out, driver_19_out, driver_29_out, imm8,
       instruction_decoder_1_p5, instruction_decoder_1_p7, IR0_D, PC_hi, PC_lo, ramdualport_1_d, SP_hi, SP_lo;
  wire [15:0] driver_1_out, driver_8_out;

  or or_1 (or_1_out, SP_DEC, SP_INC);
  LED led_1 (.in(undriven));
  microcode microcode_1 (
    .d0(IR0_D), .c(clk), .PC_INC(PC_INC), .PCL_WE(PC_L_RD), .PCH_WE(PC_H_RD), .IR0_RD(IR0_RD),
    .IR1_RD(IR1_RD), .IR2_RD(IR2_RD), .SP_INC(SP_INC), .SP_DEC(SP_DEC), .DB_RD_DEV(REG_RD),
    .DB_WR_DEV(DB_WR_DEV), .AB_WR_DEV(AB_WR_DEV), .STORE_FLAG(STORE_FLAG), .STORE_ACC(STORE_ACC),
    .MEM_WE(MEM_WE), .MEM_OE(MEM_OE));  // open: uPC_clr_2, uPC_CLR, PC_SRC, uPC_Cond_CLR, upc, addr
  Decoder #(.Selector_Bits(2)) decoder_1 (
    .sel(AB_WR_DEV), .out_1(PC_WR_ABUS), .out_2(SP_WR_ABUS), .out_3(RS_WR_ABUS));  // open: out_0
  _16_bit_presettable_counter PC (
    .en(PC_INC), .c(clk), .dir(1'b0), .lo_in(ramdualport_1_d), .lo_ld(PC_L_RD), .hi_in(ramdualport_1_d),
    .hi_ld(PC_H_RD), .clr(1'b0), .ovf(PC_ovf), .lo(PC_lo), .hi(PC_hi));
  _16_bit_presettable_counter SP (
    .en(or_1_out), .c(clk), .dir(SP_DEC), .lo_in(ramdualport_1_d), .lo_ld(SP_L_RD), .hi_in(ramdualport_1_d),
    .hi_ld(SP_H_RD), .clr(1'b0), .ovf(SP_ovf), .lo(SP_lo), .hi(SP_hi));
  LED led_2 (.in(PC_ovf));
  assign driver_1_out = PC_WR_ABUS ? {PC_hi, PC_lo} : 16'bz;  // Driver driver_1
  LED led_3 (.in(SP_ovf));
  assign driver_1_out = SP_WR_ABUS ? {SP_hi, SP_lo} : 16'bz;  // Driver driver_2
  assign driver_3_out = SP_L_WR_DB ? SP_lo : 8'bz;  // Driver driver_3
  assign driver_3_out = SP_H_WR_DB ? SP_hi : 8'bz;  // Driver driver_4
  Decoder #(.Selector_Bits(3)) decoder_2 (
    .sel(REG_RD), .out_1(RD_R_vvvv), .out_2(RD_R_rs0), .out_3(RD_R_rs1), .out_6(SP_L_RD), .out_7(SP_H_RD));  // open: out_0, out_4, out_5
  Decoder #(.Selector_Bits(3)) decoder_3 (
    .sel(DB_WR_DEV), .out_1(WR_R_vvvv), .out_2(WR_R_rs0), .out_3(WR_R_rs1), .out_6(SP_L_WR_DB),
    .out_7(SP_H_WR_DB));  // open: out_0, out_4, out_5
  // Probe DBUS on ramdualport_1_d
  // Probe ABUS on driver_1_out
  Demultiplexer demultiplexer_1 (
    .sel(driver_1_out[15]), .in(MEM_OE), .out_0(demultiplexer_1_out_0), .out_1(demultiplexer_1_out_1));
  RAMDualPort #(.AddrBits(15), .Bits(8)) ramdualport_1 (
    .A(driver_1_out[14:0]), .Din(ramdualport_1_d), .str(MEM_WE), .C(clk), .ld(demultiplexer_1_out_1),
    .D(ramdualport_1_d));
  ROM #(.AddrBits(15), .Bits(8)) rom_1 (.A(driver_1_out[14:0]), .sel(demultiplexer_1_out_0), .D(ramdualport_1_d));
  assign driver_1_out = RS_WR_ABUS ? driver_8_out : 16'bz;  // Driver driver_5
  Register #(.Bits(8)) IR0 (.D(ramdualport_1_d), .C(clk), .en(IR0_RD), .Q(IR0_D));
  Register #(.Bits(8)) A (.D(ramdualport_1_d), .C(clk), .en(REG_A_RD), .Q(A_q));
  Register #(.Bits(8)) B (.D(ramdualport_1_d), .C(clk), .en(REG_B_RD), .Q(B_q));
  Register #(.Bits(8)) C (.D(ramdualport_1_d), .C(clk), .en(REG_C_RD), .Q(C_q));
  Register #(.Bits(8)) D (.D(ramdualport_1_d), .C(clk), .en(REG_D_RD), .Q(D_q));
  // instruction_decoder instruction_decoder_1: pin names not known; wires that end beside it: MEM_OE, ll, IR0_D, ooo, instruction_decoder_1_p5, vvv, instruction_decoder_1_p7, imm8, rs0, rs1, imm16
  Register #(.Bits(8)) IR1 (.D(ramdualport_1_d), .C(clk), .en(IR1_RD), .Q(instruction_decoder_1_p5));
  assign ramdualport_1_d = A_WR_DB ? A_q : 8'bz;  // Driver driver_6
  assign driver_8_out[7:0] = ADDR_RS1_A ? A_q : 8'bz;  // Driver driver_7
  assign driver_8_out[15:8] = ADDR_RS0_A ? A_q : 8'bz;  // Driver driver_8
  assign ramdualport_1_d = B_WR_DB ? B_q : 8'bz;  // Driver driver_9
  assign driver_8_out[7:0] = ADDR_RS1_B ? B_q : 8'bz;  // Driver driver_10
  assign driver_8_out[15:8] = ADDR_RS0_B ? B_q : 8'bz;  // Driver driver_11
  assign ramdualport_1_d = C_WR_DB ? C_q : 8'bz;  // Driver driver_12
  assign driver_8_out[7:0] = ADDR_RS1_C ? C_q : 8'bz;  // Driver driver_13
  assign driver_8_out[15:8] = ADDR_RS0_C ? C_q : 8'bz;  // Driver driver_14
  assign ramdualport_1_d = D_WR_DB ? D_q : 8'bz;  // Driver driver_15
  assign driver_8_out[7:0] = ADDR_RS1_D ? D_q : 8'bz;  // Driver driver_16
  assign driver_8_out[15:8] = ADDR_RS0_D ? D_q : 8'bz;  // Driver driver_17
  Register #(.Bits(8)) IR2 (.D(ramdualport_1_d), .C(clk), .en(IR2_RD), .Q(instruction_decoder_1_p7));
  assign driver_3_out = ALU_A_IN_B ? A_q : 8'bz;  // Driver driver_18
  assign driver_19_out = ALU_A_IN_A ? A_q : 8'bz;  // Driver driver_19
  assign driver_3_out = ALU_B_IN_B ? B_q : 8'bz;  // Driver driver_20
  assign driver_19_out = ALU_B_IN_A ? B_q : 8'bz;  // Driver driver_21
  assign driver_3_out = ALU_C_IN_B ? C_q : 8'bz;  // Driver driver_22
  assign driver_19_out = ALU_C_IN_A ? C_q : 8'bz;  // Driver driver_23
  assign driver_3_out = ALU_D_IN_B ? D_q : 8'bz;  // Driver driver_24
  assign driver_19_out = ALU_D_IN_A ? D_q : 8'bz;  // Driver driver_25
  assign driver_3_out = 1'b0 ? imm8 : 8'bz;  // Driver driver_26
  alu alu_1 (.flags(Flag_q), .A(driver_19_out), .B(driver_3_out), .op(ooo), .flags_2(alu_1_flags_2), .out(alu_1_out));
  nand nand_1 (nand_1_out, ll[0], ll[1]);
  assign driver_19_out = nand_1_out ? ACC_q : 8'bz;  // Driver driver_27
  assign ramdualport_1_d = ACC_WR_DB ? ACC_q : 8'bz;  // Driver driver_28
  assign driver_29_out = REG_ACC_RD ? ramdualport_1_d : 8'bz;  // Driver driver_29
  Register #(.Bits(4)) Flag (.D(alu_1_flags_2), .C(clk), .en(STORE_FLAG), .Q(Flag_q));
  Decoder #(.Selector_Bits(2)) decoder_4 (
    .sel(vvv[1:0]), .out_0(ALU_A_IN_B), .out_1(ALU_B_IN_B), .out_2(ALU_C_IN_B), .out_3(ALU_D_IN_B));
  Decoder #(.Selector_Bits(2)) decoder_5 (
    .sel(rs0[1:0]), .out_0(ALU_A_IN_A), .out_1(ALU_B_IN_A), .out_2(ALU_C_IN_A), .out_3(ALU_D_IN_A));
  assign driver_3_out = and_1_out ? ACC_q : 8'bz;  // Driver driver_30
  write_dbus_signals write_dbus_signals_1 (
    .vvv(vvv), .rs0(rs0), .rs1(rs1), .R_vvv(RD_R_vvvv), .R_rs0(RD_R_rs0), .R_rs1(RD_R_rs1));  // open: A, B, C, D, SP_Hi, SP_Lo
  and and_1 (and_1_out, ooo[0], ~ooo[1], ~ooo[2], nand_1_out);  // And
  assign driver_29_out = not_1_out ? alu_1_out : 8'bz;  // Driver driver_31
  not not_1 (not_1_out, REG_ACC_RD);
  or or_2 (or_2_out, REG_ACC_RD, STORE_ACC);
  Register #(.Bits(8)) ACC (.D(driver_29_out), .C(clk), .en(or_2_out), .Q(ACC_q));
  write_dbus_signals write_dbus_signals_2 (
    .vvv(vvv), .rs0(rs0), .rs1(rs1), .R_vvv(WR_R_vvvv), .R_rs0(WR_R_rs0), .R_rs1(WR_R_rs1));  // open: A, B, C, D, SP_Hi, SP_Lo
  Decoder #(.Selector_Bits(2)) decoder_6 (
    .sel(rs0[1:0]), .out_0(ADDR_RS0_A), .out_1(ADDR_RS0_B), .out_2(ADDR_RS0_C), .out_3(ADDR_RS0_D));
  Decoder #(.Selector_Bits(2)) decoder_7 (
    .sel(rs1[1:0]), .out_0(ADDR_RS1_A), .out_1(ADDR_RS1_B), .out_2(ADDR_RS1_C), .out_3(ADDR_RS1_D));

  // Notes on the sheet:
  //   Stack Pointer
  //   Decoders
  //   Program Counter
  //   DBUS
  //   ABUS
  //   Instruction Register
  //   Registers
  //   Decoder
  //   ALU
  //   ALU BUS
  //   ALU Decoders
  //   ACC
  //   Flag register
  //   Register Decoders
  //   Address Decoders
endmodule
