// Digital circuit microcode.dig as structural Verilog
module microcode (
  input  [7:0] d0,
  input  c,
  input  uPC_clr_2,
  output uPC_CLR,
  output PC_INC,
  output PCL_WE,
  output PCH_WE,
  output IR0_RD,
  output IR1_RD,
  output IR2_RD,
  output SP_INC,
  output SP_DEC,
  output [2:0] DB_RD_DEV,
  output [2:0] DB_WR_DEV,
  output [1:0] AB_WR_DEV,
  output STORE_FLAG,
  output STORE_ACC,
  output MEM_WE,
  output MEM_OE,
  output [2:0] PC_SRC,
  output uPC_Cond_CLR
);

  wire or_1_out;
  wire [3:0] uPC_out;
  wire [7:1] rom_1_d;

  ROM #(.AddrBits(12), .Bits(8)) rom_1 (.A({uPC_out, d0}), .sel(1'b1), .D({rom_1_d, MEM_OE}));
  or or_1 (or_1_out, uPC_clr_2, uPC_CLR);
  ROM #(.AddrBits(12), .Bits(8)) rom_2 (
    .A({uPC_out, d0}), .sel(1'b1), .D({MEM_WE, STORE_ACC, STORE_FLAG, DB_WR_DEV, DB_RD_DEV[2:1]}));
  Counter #(.Bits(4)) uPC (.en(1'b1), .C(c), .clr(or_1_out), .out(uPC_out));  // open: ovf
  ROM #(.AddrBits(12), .Bits(8)) rom_3 (
    .A({uPC_out, d0}), .sel(1'b1), .D({DB_RD_DEV[0], AB_WR_DEV, SP_DEC, SP_INC, IR2_RD, IR1_RD, IR0_RD}));
  ROM #(.AddrBits(12), .Bits(8)) rom_4 (
    .A({uPC_out, d0}), .sel(1'b1), .D({PC_SRC, PCH_WE, PCL_WE, PC_INC, uPC_Cond_CLR, uPC_CLR}));

  // Notes on the sheet:
  //   contents of rom_3 (hex, n*v repeats v):
  //   2
  //   contents of rom_4 (hex, n*v repeats v):
  //   6,1,254*0,1
endmodule
